// Logisim project primeira_avaliacao.circ as structural Verilog
module mux16 (
  input  in_1,
  input  in_2,
  input  in_3,
  input  in_4,
  input  in_5,
  input  in_6,
  input  in_7,
  input  in_8,
  input  in_9,
  input  in_10,
  input  in_11,
  input  in_12,
  input  in_13,
  input  in_14,
  input  in_15,
  input  in_16,
  input  [3:0] Sel,
  output out_18
);

  wire and_1_out, and_2_out, and_3_out, and_4_out, and_5_out, and_6_out, and_7_out, and_8_out, and_9_out,
       and_10_out, and_11_out, and_12_out, and_13_out, and_14_out, and_15_out, and_16_out;

  and and_1 (and_1_out, in_1, ~Sel[3], ~Sel[2], ~Sel[1], ~Sel[0]);  // AND_Gate
  and and_2 (and_2_out, in_2, ~Sel[3], ~Sel[2], ~Sel[1], Sel[0]);  // AND_Gate
  and and_3 (and_3_out, in_3, ~Sel[3], ~Sel[2], Sel[1], ~Sel[0]);  // AND_Gate
  and and_4 (and_4_out, in_4, ~Sel[3], ~Sel[2], Sel[1], Sel[0]);  // AND_Gate
  and and_5 (and_5_out, in_5, ~Sel[3], Sel[2], ~Sel[1], ~Sel[0]);  // AND_Gate
  and and_6 (and_6_out, in_6, ~Sel[3], Sel[2], ~Sel[1], Sel[0]);  // AND_Gate
  and and_7 (and_7_out, in_7, ~Sel[3], Sel[2], Sel[1], ~Sel[0]);  // AND_Gate
  and and_8 (and_8_out, in_8, ~Sel[3], Sel[2], Sel[1], Sel[0]);  // AND_Gate
  and and_9 (and_9_out, in_9, Sel[3], ~Sel[2], ~Sel[1], ~Sel[0]);  // AND_Gate
  and and_10 (and_10_out, in_10, Sel[3], ~Sel[2], ~Sel[1], Sel[0]);  // AND_Gate
  and and_11 (and_11_out, in_11, Sel[3], ~Sel[2], Sel[1], ~Sel[0]);  // AND_Gate
  and and_12 (and_12_out, in_12, Sel[3], ~Sel[2], Sel[1], Sel[0]);  // AND_Gate
  and and_13 (and_13_out, in_13, Sel[3], Sel[2], ~Sel[1], ~Sel[0]);  // AND_Gate
  and and_14 (and_14_out, in_14, Sel[3], Sel[2], ~Sel[1], Sel[0]);  // AND_Gate
  and and_15 (and_15_out, in_15, Sel[3], Sel[2], Sel[1], ~Sel[0]);  // AND_Gate
  and and_16 (and_16_out, in_16, Sel[3], Sel[2], Sel[1], Sel[0]);
  or or_1 (out_18, and_1_out, and_2_out, and_3_out, and_4_out, and_5_out, and_6_out, and_7_out, and_8_out, and_9_out, and_10_out, and_11_out, and_12_out, and_13_out, and_14_out, and_15_out, and_16_out);
endmodule

module ULACell (
  input  B,
  input  A,
  input  [3:0] SelectorOperador,
  input  vem1_plus,
  input  vem1_minus,
  output \Saída ,
  output vai1_plus,
  output vai1_minus
);

  wire and_1_out, nand_1_out, or_1_out, somc_1_soma, sub_1_soma, xor_1_out;

  and and_1 (and_1_out, A, B);
  or or_1 (or_1_out, A, B);
  xor xor_1 (xor_1_out, A, B);
  SomC somc_1 (.Vai1(vai1_plus), .B(B), .A(A), .Soma(somc_1_soma), .V1(vem1_plus));
  Sub sub_1 (.Vai1(vai1_minus), .B(B), .A(A), .Soma(sub_1_soma), .V1(vem1_minus));
  nand nand_1 (nand_1_out, A, B);
  mux16 mux16_1 (
    .in_1(and_1_out), .in_2(or_1_out), .in_3(xor_1_out), .in_4(somc_1_soma), .in_5(sub_1_soma), .in_6(B),
    .in_7(B), .in_8(B), .in_9(B), .in_10(nand_1_out), .in_11(B), .Sel(SelectorOperador), .out_18(\Saída ));  // open: in_12, in_13, in_14, in_15, in_16
endmodule

module SomC (
  input  B,
  input  A,
  input  V1,
  output Vai1,
  output Soma
);

  wire and_1_out, and_2_out, and_3_out, xor_1_out;

  or or_1 (Vai1, and_1_out, and_2_out, and_3_out);
  and and_1 (and_1_out, V1, B);
  and and_2 (and_2_out, B, A);
  and and_3 (and_3_out, A, V1);
  xor xor_1 (xor_1_out, A, B);
  xor xor_2 (Soma, xor_1_out, V1);
endmodule

module ULA (
  input  [31:0] A,
  input  [31:0] B,
  input  [3:0] in_3,
  output out_4,
  output out_5,
  output [31:0] out_6
);

  wire lua_detector_1_out_2, sleft1bit_detector_1_out_2, sright1bit_detector_1_out_2,
       srighta1bit_detector_1_out_2, ulacell_1_p7, ulacell_1_p8, ulacell_2_p7, ulacell_2_p8, ulacell_3_p7,
       ulacell_3_p8, ulacell_4_p7, ulacell_4_p8, ulacell_5_p7, ulacell_5_p8, ulacell_6_p7, ulacell_6_p8,
       ulacell_7_p7, ulacell_7_p8, ulacell_8_p7, ulacell_8_p8, ulacell_9_p7, ulacell_9_p8, ulacell_10_p7,
       ulacell_10_p8, ulacell_11_p7, ulacell_11_p8, ulacell_12_p7, ulacell_12_p8, ulacell_13_p7,
       ulacell_13_p8, ulacell_14_p1, ulacell_14_p2, ulacell_14_p7, ulacell_14_p8, ulacell_16_p7,
       ulacell_16_p8, ulacell_17_p7, ulacell_17_p8, ulacell_18_p7, ulacell_18_p8, ulacell_19_p7,
       ulacell_19_p8, ulacell_20_p7, ulacell_20_p8, ulacell_21_p7, ulacell_21_p8, ulacell_22_p7,
       ulacell_22_p8, ulacell_23_p7, ulacell_23_p8, ulacell_24_p7, ulacell_24_p8, ulacell_25_p7,
       ulacell_25_p8, ulacell_26_p1, ulacell_26_p2, ulacell_26_p7, ulacell_26_p8, ulacell_28_p7,
       ulacell_28_p8, ulacell_29_p7, ulacell_29_p8, ulacell_30_p1, ulacell_30_p2, ulacell_30_p7,
       ulacell_30_p8;
  wire [31:0] lua_1_out_3, sleftl1bit_1_out_3, srighta1bit_1_out_3, srightl1bit_1_out_3;

  SleftL1bit sleftl1bit_1 (.in_1(B), .Shift(sleft1bit_detector_1_out_2), .out_3(sleftl1bit_1_out_3));
  Sleft1bit_detector sleft1bit_detector_1 (.out_2(sleft1bit_detector_1_out_2), .in_1(in_3));
  Sright1bit_detector sright1bit_detector_1 (.out_2(sright1bit_detector_1_out_2), .in_1(in_3));
  SrightL1bit srightl1bit_1 (
    .in_1(sleftl1bit_1_out_3), .Shift(sright1bit_detector_1_out_2), .out_3(srightl1bit_1_out_3));
  SrightA1bit srighta1bit_1 (
    .in_1(srightl1bit_1_out_3), .Shift(srighta1bit_detector_1_out_2), .out_3(srighta1bit_1_out_3));
  SrightA1bit_detector srighta1bit_detector_1 (.out_2(srighta1bit_detector_1_out_2), .in_1(in_3));
  LUA_detector lua_detector_1 (.out_2(lua_detector_1_out_2), .in_1(in_3));
  LUA lua_1 (.in_1(srighta1bit_1_out_3), .Shift(lua_detector_1_out_2), .out_3(lua_1_out_3));
  // ULACell ulacell_1: pin names not known; wires that end beside it: out_4, out_5, lua_1_out_3[31], in_3, A[31], out_6[31], ulacell_1_p7, ulacell_1_p8
  // ULACell ulacell_2: pin names not known; wires that end beside it: ulacell_1_p7, ulacell_1_p8, lua_1_out_3[30], in_3, A[30], out_6[30], ulacell_2_p7, ulacell_2_p8
  // ULACell ulacell_3: pin names not known; wires that end beside it: ulacell_2_p7, ulacell_2_p8, lua_1_out_3[29], in_3, A[29], out_6[29], ulacell_3_p7, ulacell_3_p8
  // ULACell ulacell_4: pin names not known; wires that end beside it: ulacell_3_p7, ulacell_3_p8, lua_1_out_3[28], in_3, A[28], out_6[28], ulacell_4_p7, ulacell_4_p8
  // ULACell ulacell_5: pin names not known; wires that end beside it: ulacell_4_p7, ulacell_4_p8, lua_1_out_3[27], in_3, A[27], out_6[27], ulacell_5_p7, ulacell_5_p8
  // ULACell ulacell_6: pin names not known; wires that end beside it: ulacell_5_p7, ulacell_5_p8, lua_1_out_3[26], in_3, A[26], out_6[26], ulacell_6_p7, ulacell_6_p8
  // ULACell ulacell_7: pin names not known; wires that end beside it: ulacell_6_p7, ulacell_6_p8, lua_1_out_3[25], in_3, A[25], out_6[25], ulacell_7_p7, ulacell_7_p8
  // ULACell ulacell_8: pin names not known; wires that end beside it: ulacell_7_p7, ulacell_7_p8, lua_1_out_3[24], in_3, A[24], out_6[24], ulacell_8_p7, ulacell_8_p8
  // ULACell ulacell_9: pin names not known; wires that end beside it: ulacell_8_p7, ulacell_8_p8, lua_1_out_3[23], in_3, A[23], out_6[23], ulacell_9_p7, ulacell_9_p8
  // ULACell ulacell_10: pin names not known; wires that end beside it: ulacell_9_p7, ulacell_9_p8, lua_1_out_3[22], in_3, A[22], out_6[22], ulacell_10_p7, ulacell_10_p8
  // ULACell ulacell_11: pin names not known; wires that end beside it: ulacell_10_p7, ulacell_10_p8, lua_1_out_3[21], in_3, A[21], out_6[21], ulacell_11_p7, ulacell_11_p8
  // ULACell ulacell_12: pin names not known; wires that end beside it: ulacell_11_p7, ulacell_11_p8, lua_1_out_3[20], in_3, A[20], out_6[20], ulacell_12_p7, ulacell_12_p8
  // ULACell ulacell_13: pin names not known; wires that end beside it: ulacell_12_p7, ulacell_12_p8, lua_1_out_3[19], in_3, A[19], out_6[19], ulacell_13_p7, ulacell_13_p8
  // ULACell ulacell_14: pin names not known; wires that end beside it: ulacell_14_p1, ulacell_14_p2, lua_1_out_3[17], in_3, A[17], out_6[17], ulacell_14_p7, ulacell_14_p8
  // ULACell ulacell_15: pin names not known; wires that end beside it: ulacell_13_p7, ulacell_13_p8, lua_1_out_3[18], in_3, A[18], out_6[18], ulacell_14_p1, ulacell_14_p2
  // ULACell ulacell_16: pin names not known; wires that end beside it: ulacell_14_p7, ulacell_14_p8, lua_1_out_3[16], in_3, A[16], out_6[16], ulacell_16_p7, ulacell_16_p8
  // ULACell ulacell_17: pin names not known; wires that end beside it: ulacell_16_p7, ulacell_16_p8, lua_1_out_3[15], in_3, A[15], out_6[15], ulacell_17_p7, ulacell_17_p8
  // ULACell ulacell_18: pin names not known; wires that end beside it: ulacell_17_p7, ulacell_17_p8, lua_1_out_3[14], in_3, A[14], out_6[14], ulacell_18_p7, ulacell_18_p8
  // ULACell ulacell_19: pin names not known; wires that end beside it: ulacell_18_p7, ulacell_18_p8, lua_1_out_3[13], in_3, A[13], out_6[13], ulacell_19_p7, ulacell_19_p8
  // ULACell ulacell_20: pin names not known; wires that end beside it: ulacell_19_p7, ulacell_19_p8, lua_1_out_3[12], in_3, A[12], out_6[12], ulacell_20_p7, ulacell_20_p8
  // ULACell ulacell_21: pin names not known; wires that end beside it: ulacell_20_p7, ulacell_20_p8, lua_1_out_3[11], in_3, A[11], out_6[11], ulacell_21_p7, ulacell_21_p8
  // ULACell ulacell_22: pin names not known; wires that end beside it: ulacell_21_p7, ulacell_21_p8, lua_1_out_3[10], in_3, A[10], out_6[10], ulacell_22_p7, ulacell_22_p8
  // ULACell ulacell_23: pin names not known; wires that end beside it: ulacell_22_p7, ulacell_22_p8, lua_1_out_3[9], in_3, A[9], out_6[9], ulacell_23_p7, ulacell_23_p8
  // ULACell ulacell_24: pin names not known; wires that end beside it: ulacell_23_p7, ulacell_23_p8, lua_1_out_3[8], in_3, A[8], out_6[8], ulacell_24_p7, ulacell_24_p8
  // ULACell ulacell_25: pin names not known; wires that end beside it: ulacell_24_p7, ulacell_24_p8, lua_1_out_3[7], in_3, A[7], out_6[7], ulacell_25_p7, ulacell_25_p8
  // ULACell ulacell_26: pin names not known; wires that end beside it: ulacell_26_p1, ulacell_26_p2, lua_1_out_3[5], in_3, A[5], out_6[5], ulacell_26_p7, ulacell_26_p8
  // ULACell ulacell_27: pin names not known; wires that end beside it: ulacell_25_p7, ulacell_25_p8, lua_1_out_3[6], in_3, A[6], out_6[6], ulacell_26_p1, ulacell_26_p2
  // ULACell ulacell_28: pin names not known; wires that end beside it: ulacell_26_p7, ulacell_26_p8, lua_1_out_3[4], in_3, A[4], out_6[4], ulacell_28_p7, ulacell_28_p8
  // ULACell ulacell_29: pin names not known; wires that end beside it: ulacell_28_p7, ulacell_28_p8, lua_1_out_3[3], in_3, A[3], out_6[3], ulacell_29_p7, ulacell_29_p8
  // ULACell ulacell_30: pin names not known; wires that end beside it: ulacell_30_p1, ulacell_30_p2, lua_1_out_3[1], in_3, A[1], out_6[1], ulacell_30_p7, ulacell_30_p8
  // ULACell ulacell_31: pin names not known; wires that end beside it: ulacell_29_p7, ulacell_29_p8, lua_1_out_3[2], in_3, A[2], out_6[2], ulacell_30_p1, ulacell_30_p2
  // ULACell ulacell_32: pin names not known; wires that end beside it: ulacell_30_p7, ulacell_30_p8, lua_1_out_3[0], in_3, A[0], out_6[0], 1'b0, 1'b0
endmodule

module Sub (
  input  B,
  input  A,
  input  V1,
  output Vai1,
  output Soma
);

  wire and_1_out, and_2_out, and_3_out, xor_1_out;

  or or_1 (Vai1, and_1_out, and_2_out, and_3_out);
  and and_1 (and_1_out, V1, B);
  and and_2 (and_2_out, B, ~A);  // AND_Gate
  and and_3 (and_3_out, ~A, V1);  // AND_Gate
  xor xor_1 (xor_1_out, A, B);
  xor xor_2 (Soma, xor_1_out, V1);
endmodule

module SleftL1bit (
  input  [31:0] in_1,
  input  Shift,
  output [31:0] out_3
);

  Multiplexer #(.width(32), .enable("false")) multiplexer_1 (
    .in0(in_1), .in1({in_1[30:0], 1'b0}), .out(out_3), .sel(Shift));
endmodule

module SrightL1bit (
  input  [31:0] in_1,
  input  Shift,
  output [31:0] out_3
);

  Multiplexer #(.width(32), .enable("false")) multiplexer_1 (
    .in0(in_1), .in1({1'b0, in_1[31:1]}), .out(out_3), .sel(Shift));
endmodule

module SrightA1bit (
  input  [31:0] in_1,
  input  Shift,
  output [31:0] out_3
);

  Multiplexer #(.width(32), .enable("false")) multiplexer_1 (
    .in0(in_1), .in1({{2{in_1[31]}}, in_1[30:1]}), .out(out_3), .sel(Shift));
endmodule

module SleftA1bit (
  input  [31:0] in_1,
  input  Shift,
  output [31:0] out_3
);

  Multiplexer #(.width(32), .enable("false")) multiplexer_1 (
    .in0(in_1), .in1({in_1[30:0], in_1[0]}), .out(out_3), .sel(Shift));
endmodule

module Sleft1bit_detector (
  input  [3:0] in_1,
  output out_2
);

  and and_1 (out_2, ~in_1[3], in_1[2], in_1[1], ~in_1[0]);  // AND_Gate
endmodule

module Sright1bit_detector (
  input  [3:0] in_1,
  output out_2
);

  and and_1 (out_2, ~in_1[3], in_1[2], in_1[1], in_1[0]);  // AND_Gate
endmodule

module SrightA1bit_detector (
  input  [3:0] in_1,
  output out_2
);

  and and_1 (out_2, in_1[3], ~in_1[2], ~in_1[1], ~in_1[0]);  // AND_Gate
endmodule

module LUA (
  input  [31:0] in_1,
  input  Shift,
  output [31:0] out_3
);

  Multiplexer #(.width(32), .enable("false")) multiplexer_1 (
    .in0(in_1),
    .in1({in_1[0], in_1[1], in_1[2], in_1[3], in_1[4], in_1[5], in_1[6], in_1[7], in_1[8], in_1[9], in_1[10], in_1[11], in_1[12], in_1[13], in_1[14], in_1[15], {16{1'b0}}}),
    .out(out_3), .sel(Shift));
endmodule

module LUA_detector (
  input  [3:0] in_1,
  output out_2
);

  and and_1 (out_2, in_1[3], ~in_1[2], in_1[1], ~in_1[0]);  // AND_Gate
endmodule
