// Logisim project ula-reg.circ as structural Verilog
module mux2 (
  input  in_1,
  input  in_2,
  input  SelM2,
  output out_4
);

  wire and_1_out, and_2_out;

  and and_1 (and_1_out, in_1, ~SelM2);  // AND_Gate
  and and_2 (and_2_out, in_2, SelM2);
  or or_1 (out_4, and_1_out, and_2_out);
endmodule

module mux8 (
  input  in_1,
  input  in_2,
  input  in_3,
  input  in_4,
  input  in_5,
  input  in_6,
  input  in_7,
  input  in_8,
  input  [2:0] SelM8,
  output out_10
);

  wire and_1_out, and_2_out, and_3_out, and_4_out, and_5_out, and_6_out, and_7_out, and_8_out;

  and and_1 (and_1_out, in_1, ~SelM8[2], ~SelM8[1], ~SelM8[0]);  // AND_Gate
  and and_2 (and_2_out, in_2, ~SelM8[2], ~SelM8[1], SelM8[0]);  // AND_Gate
  and and_3 (and_3_out, in_3, ~SelM8[2], SelM8[1], ~SelM8[0]);  // AND_Gate
  and and_4 (and_4_out, in_4, ~SelM8[2], SelM8[1], SelM8[0]);  // AND_Gate
  and and_5 (and_5_out, in_5, SelM8[2], ~SelM8[1], ~SelM8[0]);  // AND_Gate
  and and_6 (and_6_out, in_6, SelM8[2], SelM8[1], ~SelM8[0]);  // AND_Gate
  and and_7 (and_7_out, in_7, SelM8[2], ~SelM8[1], SelM8[0]);  // AND_Gate
  and and_8 (and_8_out, in_8, SelM8[2], SelM8[1], SelM8[0]);
  or or_1 (out_10, and_1_out, and_2_out, and_3_out, and_4_out, and_5_out, and_6_out, and_7_out, and_8_out);
endmodule

module mux16 (
  input  [7:0] in_1,
  input  [7:0] in_2,
  input  [3:0] selM16,
  output out_4
);

  wire mux8_1_out_10, mux8_2_out_10;

  mux8 mux8_1 (
    .in_1(in_1[0]), .in_2(in_1[1]), .in_3(in_1[2]), .in_4(in_1[3]), .in_5(in_1[4]), .in_6(in_1[5]),
    .in_7(in_1[6]), .in_8(in_1[7]), .out_10(mux8_1_out_10), .SelM8(selM16[2:0]));
  mux8 mux8_2 (
    .in_1(in_2[0]), .in_2(in_2[1]), .in_3(in_2[2]), .in_4(in_2[3]), .in_5(in_2[4]), .in_6(in_2[5]),
    .in_7(in_2[6]), .in_8(in_2[7]), .out_10(mux8_2_out_10), .SelM8(selM16[2:0]));
  mux2 mux2_1 (.in_1(mux8_1_out_10), .in_2(mux8_2_out_10), .out_4(out_4), .SelM2(selM16[3]));
endmodule

module Somador_Completo (
  input  Vem1,
  input  a,
  input  b,
  output Soma,
  output Vai1
);

  wire and_1_out, and_2_out, and_3_out, xor_1_out;

  xor xor_1 (xor_1_out, a, b);
  and and_1 (and_1_out, a, Vem1);
  and and_2 (and_2_out, a, b);
  and and_3 (and_3_out, b, Vem1);
  xor xor_2 (Soma, Vem1, xor_1_out);
  or or_1 (Vai1, and_1_out, and_2_out, and_3_out);
endmodule

module ULAcell (
  input  B,
  input  A,
  input  [3:0] OperCode,
  input  Vem1,
  input  NegarB,
  output \Saída ,
  output Vai1
);

  wire mux2_1_out_4, not_1_out;
  wire [3:0] and_1_out;
  wire [7:1] nand_1_out;

  mux2 mux2_1 (.in_1(B), .in_2(not_1_out), .out_4(mux2_1_out_4), .SelM2(NegarB));
  not not_1 (not_1_out, B);
  nand nand_1 (nand_1_out[1], B, A);
  Somador_Completo somador_completo_1 (.Vem1(Vem1), .a(A), .b(mux2_1_out_4), .Soma(and_1_out[3]), .Vai1(Vai1));
  and and_1 (and_1_out[0], B, A);
  or or_1 (and_1_out[1], B, A);
  xor xor_1 (and_1_out[2], B, A);
  mux16 mux16_1 (
    .in_1({{4{B}}, and_1_out}), .in_2({nand_1_out[7:3], and_1_out[3], nand_1_out[1], A}), .out_4(\Saída ),
    .selM16(OperCode));
endmodule

module sll1bit (
  input  [31:0] Entrada,
  input  Shift,
  output [31:0] \Saída 
);

  Multiplexer #(.width(32), .enable("false")) multiplexer_1 (
    .in0(Entrada), .in1({Entrada[30:0], 1'b0}), .out(\Saída ), .sel(Shift));
endmodule

module sll1bit_detector (
  input  [3:0] OperCOde,
  output \Saída 
);

  and and_1 (\Saída , ~OperCOde[3], OperCOde[2], ~OperCOde[1], OperCOde[0]);  // AND_Gate
endmodule

module srl1bit (
  input  [31:0] Entrada,
  input  Shift,
  output [31:0] \Saída 
);

  Multiplexer #(.width(32), .enable("false")) multiplexer_1 (
    .in0(Entrada), .in1({1'b0, Entrada[31:1]}), .out(\Saída ), .sel(Shift));
endmodule

module srl1bit_detector (
  input  [3:0] OperCOde,
  output \Saída 
);

  and and_1 (\Saída , ~OperCOde[3], OperCOde[2], OperCOde[1], ~OperCOde[0]);  // AND_Gate
endmodule

module sra1bit (
  input  [31:0] Entrada,
  input  Shift,
  output [31:0] \Saída 
);

  Multiplexer #(.width(32), .enable("false")) multiplexer_1 (
    .in0(Entrada), .in1({{2{Entrada[31]}}, Entrada[30:1]}), .out(\Saída ), .sel(Shift));
endmodule

module sra_detector (
  input  [3:0] OperCOde,
  output \Saída 
);

  and and_1 (\Saída , ~OperCOde[3], OperCOde[2], OperCOde[1], OperCOde[0]);  // AND_Gate
endmodule

module lua16bits (
  input  [31:0] Entrada,
  input  Shift,
  output [31:0] Entrada_2
);

  Multiplexer #(.width(32), .enable("false")) multiplexer_1 (
    .in0(Entrada),
    .in1({Entrada[0], Entrada[1], Entrada[2], Entrada[3], Entrada[4], Entrada[5], Entrada[6], Entrada[7], Entrada[8], Entrada[9], Entrada[10], Entrada[11], Entrada[12], Entrada[13], Entrada[14], Entrada[15], {16{1'b0}}}),
    .out(Entrada_2), .sel(Shift));
endmodule

module lua_detector (
  input  [3:0] OperCOde,
  output \Saída 
);

  and and_1 (\Saída , OperCOde[3], ~OperCOde[2], ~OperCOde[1], ~OperCOde[0]);  // AND_Gate
endmodule

module subC_detector (
  input  [3:0] OperCOde,
  output \Saída 
);

  and and_1 (\Saída , OperCOde[3], ~OperCOde[2], OperCOde[1], ~OperCOde[0]);  // AND_Gate
endmodule

module ULA (
  input  [31:0] A,
  input  [31:0] B,
  input  [3:0] OperCode,
  output [31:0] \Saída ,
  output out_5
);

  wire A0, A1, A2, A3, A4, A5, A6, A7, A8, A9, A10, A11, A12, A13, A14, A15, A16, A17, A18, A19, A20, A21,
       A22, A23, A24, A25, A26, A27, A28, A29, A30, A31, B0, B1, B2, B3, B4, B5, B6, B7, B8, B9, B10, B11,
       B12, B13, B14, B15, B16, B17, B18, B19, B20, B21, B22, B23, B24, B25, B26, B27, B28, B29, B30, B31,
       \lua_detector_1_saída , \sll1bit_detector_1_saída , \sra_detector_1_saída ,
       \srl1bit_detector_1_saída , \subc_detector_1_saída , ulacell_1_vai1, ulacell_2_vai1, ulacell_3_vai1,
       ulacell_4_vai1, ulacell_5_vai1, ulacell_6_vai1, ulacell_7_vai1, ulacell_8_vai1, ulacell_9_vai1,
       ulacell_10_vai1, ulacell_11_vai1, ulacell_12_vai1, ulacell_13_vai1, ulacell_14_vai1, ulacell_15_vai1,
       ulacell_16_vai1, ulacell_17_vai1, ulacell_18_vai1, ulacell_19_vai1, ulacell_20_vai1, ulacell_21_vai1,
       ulacell_22_vai1, ulacell_23_vai1, ulacell_24_vai1, ulacell_25_vai1, ulacell_26_vai1, ulacell_27_vai1,
       ulacell_28_vai1, ulacell_29_vai1, ulacell_30_vai1, ulacell_31_vai1;
  wire [31:0] \sll1bit_1_saída , \srl1bit_1_saída ;

  ULAcell ulacell_1 (
    .Vai1(ulacell_1_vai1), .\Saída (\Saída [15]), .Vem1(ulacell_3_vai1), .B(A15), .A(A15),
    .OperCode(OperCode), .NegarB(\subc_detector_1_saída ));
  ULAcell ulacell_2 (
    .Vai1(ulacell_2_vai1), .\Saída (\Saída [16]), .Vem1(ulacell_1_vai1), .B(B16), .A(A16),
    .OperCode(OperCode), .NegarB(\subc_detector_1_saída ));
  ULAcell ulacell_3 (
    .Vai1(ulacell_3_vai1), .\Saída (\Saída [14]), .Vem1(ulacell_5_vai1), .B(B14), .A(A14),
    .OperCode(OperCode), .NegarB(\subc_detector_1_saída ));
  ULAcell ulacell_4 (
    .Vai1(ulacell_4_vai1), .\Saída (\Saída [17]), .Vem1(ulacell_2_vai1), .B(B17), .A(A17),
    .OperCode(OperCode), .NegarB(\subc_detector_1_saída ));
  ULAcell ulacell_5 (
    .Vai1(ulacell_5_vai1), .\Saída (\Saída [13]), .Vem1(ulacell_7_vai1), .B(B13), .A(A13),
    .OperCode(OperCode), .NegarB(\subc_detector_1_saída ));
  ULAcell ulacell_6 (
    .Vai1(ulacell_6_vai1), .\Saída (\Saída [18]), .Vem1(ulacell_4_vai1), .B(B18), .A(A18),
    .OperCode(OperCode), .NegarB(\subc_detector_1_saída ));
  lua16bits lua16bits_1 (
    .Entrada(A),
    .Entrada_2({A31, A30, A29, A28, A27, A26, A25, A24, A23, A22, A21, A20, A19, A18, A17, A16, A15, A14, A13, A12, A11, A10, A9, A8, A7, A6, A5, A4, A3, A2, A1, A0}),
    .Shift(\lua_detector_1_saída ));
  lua_detector lua_detector_1 (.\Saída (\lua_detector_1_saída ), .OperCOde(OperCode));
  ULAcell ulacell_7 (
    .Vai1(ulacell_7_vai1), .\Saída (\Saída [12]), .Vem1(ulacell_9_vai1), .B(B12), .A(A12),
    .OperCode(OperCode), .NegarB(\subc_detector_1_saída ));
  ULAcell ulacell_8 (
    .Vai1(ulacell_8_vai1), .\Saída (\Saída [19]), .Vem1(ulacell_6_vai1), .B(B19), .A(A19),
    .OperCode(OperCode), .NegarB(\subc_detector_1_saída ));
  ULAcell ulacell_9 (
    .Vai1(ulacell_9_vai1), .\Saída (\Saída [11]), .Vem1(ulacell_11_vai1), .B(B11), .A(A11),
    .OperCode(OperCode), .NegarB(\subc_detector_1_saída ));
  ULAcell ulacell_10 (
    .Vai1(ulacell_10_vai1), .\Saída (\Saída [20]), .Vem1(ulacell_8_vai1), .B(B20), .A(A20),
    .OperCode(OperCode), .NegarB(\subc_detector_1_saída ));
  ULAcell ulacell_11 (
    .Vai1(ulacell_11_vai1), .\Saída (\Saída [10]), .Vem1(ulacell_13_vai1), .B(B10), .A(A10),
    .OperCode(OperCode), .NegarB(\subc_detector_1_saída ));
  ULAcell ulacell_12 (
    .Vai1(ulacell_12_vai1), .\Saída (\Saída [21]), .Vem1(ulacell_10_vai1), .B(B21), .A(A21),
    .OperCode(OperCode), .NegarB(\subc_detector_1_saída ));
  sra1bit sra1bit_1 (
    .Entrada(\srl1bit_1_saída ),
    .\Saída ({B31, B30, B29, B28, B27, B26, B25, B24, B23, B22, B21, B20, B19, B18, B17, B16, B15, B14, B13, B12, B11, B10, B9, B8, B7, B6, B5, B4, B3, B2, B1, B0}),
    .Shift(\sra_detector_1_saída ));
  sra_detector sra_detector_1 (.\Saída (\sra_detector_1_saída ), .OperCOde(OperCode));
  ULAcell ulacell_13 (
    .Vai1(ulacell_13_vai1), .\Saída (\Saída [9]), .Vem1(ulacell_15_vai1), .B(B9), .A(A9),
    .OperCode(OperCode), .NegarB(\subc_detector_1_saída ));
  ULAcell ulacell_14 (
    .Vai1(ulacell_14_vai1), .\Saída (\Saída [22]), .Vem1(ulacell_12_vai1), .B(B22), .A(A22),
    .OperCode(OperCode), .NegarB(\subc_detector_1_saída ));
  sll1bit sll1bit_1 (.Entrada(B), .\Saída (\sll1bit_1_saída ), .Shift(\sll1bit_detector_1_saída ));
  srl1bit srl1bit_1 (.Entrada(\sll1bit_1_saída ), .\Saída (\srl1bit_1_saída ), .Shift(\srl1bit_detector_1_saída ));
  sll1bit_detector sll1bit_detector_1 (.\Saída (\sll1bit_detector_1_saída ), .OperCOde(OperCode));
  srl1bit_detector srl1bit_detector_1 (.\Saída (\srl1bit_detector_1_saída ), .OperCOde(OperCode));
  ULAcell ulacell_15 (
    .Vai1(ulacell_15_vai1), .\Saída (\Saída [8]), .Vem1(ulacell_17_vai1), .B(B8), .A(A8),
    .OperCode(OperCode), .NegarB(\subc_detector_1_saída ));
  ULAcell ulacell_16 (
    .Vai1(ulacell_16_vai1), .\Saída (\Saída [23]), .Vem1(ulacell_14_vai1), .B(B23), .A(A23),
    .OperCode(OperCode), .NegarB(\subc_detector_1_saída ));
  ULAcell ulacell_17 (
    .Vai1(ulacell_17_vai1), .\Saída (\Saída [7]), .Vem1(ulacell_19_vai1), .B(B7), .A(A7),
    .OperCode(OperCode), .NegarB(\subc_detector_1_saída ));
  ULAcell ulacell_18 (
    .Vai1(ulacell_18_vai1), .\Saída (\Saída [24]), .Vem1(ulacell_16_vai1), .B(B24), .A(A24),
    .OperCode(OperCode), .NegarB(\subc_detector_1_saída ));
  ULAcell ulacell_19 (
    .Vai1(ulacell_19_vai1), .\Saída (\Saída [6]), .Vem1(ulacell_21_vai1), .B(B6), .A(A6),
    .OperCode(OperCode), .NegarB(\subc_detector_1_saída ));
  ULAcell ulacell_20 (
    .Vai1(ulacell_20_vai1), .\Saída (\Saída [25]), .Vem1(ulacell_18_vai1), .B(B25), .A(A25),
    .OperCode(OperCode), .NegarB(\subc_detector_1_saída ));
  ULAcell ulacell_21 (
    .Vai1(ulacell_21_vai1), .\Saída (\Saída [5]), .Vem1(ulacell_23_vai1), .B(B5), .A(A5),
    .OperCode(OperCode), .NegarB(\subc_detector_1_saída ));
  ULAcell ulacell_22 (
    .Vai1(ulacell_22_vai1), .\Saída (\Saída [26]), .Vem1(ulacell_20_vai1), .B(B26), .A(A26),
    .OperCode(OperCode), .NegarB(\subc_detector_1_saída ));
  ULAcell ulacell_23 (
    .Vai1(ulacell_23_vai1), .\Saída (\Saída [4]), .Vem1(ulacell_25_vai1), .B(B4), .A(A4),
    .OperCode(OperCode), .NegarB(\subc_detector_1_saída ));
  ULAcell ulacell_24 (
    .Vai1(ulacell_24_vai1), .\Saída (\Saída [27]), .Vem1(ulacell_22_vai1), .B(B27), .A(A27),
    .OperCode(OperCode), .NegarB(\subc_detector_1_saída ));
  ULAcell ulacell_25 (
    .Vai1(ulacell_25_vai1), .\Saída (\Saída [3]), .Vem1(ulacell_27_vai1), .B(B3), .A(A3),
    .OperCode(OperCode), .NegarB(\subc_detector_1_saída ));
  ULAcell ulacell_26 (
    .Vai1(ulacell_26_vai1), .\Saída (\Saída [28]), .Vem1(ulacell_24_vai1), .B(B28), .A(A28),
    .OperCode(OperCode), .NegarB(\subc_detector_1_saída ));
  ULAcell ulacell_27 (
    .Vai1(ulacell_27_vai1), .\Saída (\Saída [2]), .Vem1(ulacell_29_vai1), .B(B2), .A(A2),
    .OperCode(OperCode), .NegarB(\subc_detector_1_saída ));
  ULAcell ulacell_28 (
    .Vai1(ulacell_28_vai1), .\Saída (\Saída [29]), .Vem1(ulacell_26_vai1), .B(B29), .A(A29),
    .OperCode(OperCode), .NegarB(\subc_detector_1_saída ));
  ULAcell ulacell_29 (
    .Vai1(ulacell_29_vai1), .\Saída (\Saída [1]), .Vem1(ulacell_31_vai1), .B(B1), .A(A1),
    .OperCode(OperCode), .NegarB(\subc_detector_1_saída ));
  ULAcell ulacell_30 (
    .Vai1(ulacell_30_vai1), .\Saída (\Saída [30]), .Vem1(ulacell_28_vai1), .B(B30), .A(A30),
    .OperCode(OperCode), .NegarB(\subc_detector_1_saída ));
  subC_detector subc_detector_1 (.\Saída (\subc_detector_1_saída ), .OperCOde(OperCode));
  ULAcell ulacell_31 (
    .Vai1(ulacell_31_vai1), .\Saída (\Saída [0]), .Vem1(\subc_detector_1_saída ), .B(B0), .A(A0),
    .OperCode(OperCode), .NegarB(\subc_detector_1_saída ));
  ULAcell ulacell_32 (
    .Vai1(out_5), .\Saída (\Saída [31]), .Vem1(ulacell_30_vai1), .B(B31), .A(A31), .OperCode(OperCode),
    .NegarB(\subc_detector_1_saída ));

  // Other names for the same wires on the sheet: S0 = \Saída [0]; S1 = \Saída [1]; S2 = \Saída [2]; S3 = \Saída [3];
  //   S4 = \Saída [4]; S5 = \Saída [5]; S6 = \Saída [6]; S7 = \Saída [7]; S8 = \Saída [8]; S9 = \Saída [9];
  //   S10 = \Saída [10]; S11 = \Saída [11]; S12 = \Saída [12]; S13 = \Saída [13]; S14 = \Saída [14];
  //   S15 = \Saída [15]; S16 = \Saída [16]; S17 = \Saída [17]; S18 = \Saída [18]; S19 = \Saída [19];
  //   S20 = \Saída [20]; S21 = \Saída [21]; S22 = \Saída [22]; S23 = \Saída [23]; S24 = \Saída [24];
  //   S25 = \Saída [25]; S26 = \Saída [26]; S27 = \Saída [27]; S28 = \Saída [28]; S29 = \Saída [29];
  //   S30 = \Saída [30]; S31 = \Saída [31]
endmodule

module registrador32bits (
  input  [31:0] Entrada,
  input  WR,
  output [31:0] \Saída 
);

  wire _14;

  D_Flip_Flop d_ff_1 (.clk(WR), .D(Entrada[0]), .Q(\Saída [0]));  // open: Qn, preset, en, reset
  D_Flip_Flop d_ff_2 (.clk(WR), .D(Entrada[8]), .Q(\Saída [8]));  // open: Qn, preset, en, reset
  D_Flip_Flop d_ff_3 (.clk(WR), .D(Entrada[16]), .Q(\Saída [16]));  // open: Qn, preset, en, reset
  D_Flip_Flop d_ff_4 (.clk(WR), .D(Entrada[24]), .Q(\Saída [24]));  // open: Qn, preset, en, reset
  D_Flip_Flop d_ff_5 (.clk(WR), .D(Entrada[1]), .Q(\Saída [1]));  // open: Qn, preset, en, reset
  D_Flip_Flop d_ff_6 (.clk(WR), .D(Entrada[9]), .Q(\Saída [9]));  // open: Qn, preset, en, reset
  D_Flip_Flop d_ff_7 (.clk(WR), .D(Entrada[17]), .Q(\Saída [17]));  // open: Qn, preset, en, reset
  D_Flip_Flop d_ff_8 (.clk(WR), .D(Entrada[25]), .Q(\Saída [25]));  // open: Qn, preset, en, reset
  D_Flip_Flop d_ff_9 (.clk(WR), .D(Entrada[2]), .Q(\Saída [2]));  // open: Qn, preset, en, reset
  D_Flip_Flop d_ff_10 (.clk(WR), .D(Entrada[10]), .Q(\Saída [10]));  // open: Qn, preset, en, reset
  D_Flip_Flop d_ff_11 (.clk(WR), .D(Entrada[18]), .Q(\Saída [18]));  // open: Qn, preset, en, reset
  D_Flip_Flop d_ff_12 (.clk(WR), .D(Entrada[26]), .Q(\Saída [26]));  // open: Qn, preset, en, reset
  D_Flip_Flop d_ff_13 (.clk(WR), .D(Entrada[3]), .Q(\Saída [3]));  // open: Qn, preset, en, reset
  D_Flip_Flop d_ff_14 (.clk(WR), .D(Entrada[11]), .Q(\Saída [11]));  // open: Qn, preset, en, reset
  D_Flip_Flop d_ff_15 (.clk(WR), .D(Entrada[19]), .Q(\Saída [19]));  // open: Qn, preset, en, reset
  D_Flip_Flop d_ff_16 (.clk(WR), .D(Entrada[27]), .Q(\Saída [27]));  // open: Qn, preset, en, reset
  D_Flip_Flop d_ff_17 (.clk(WR), .D(Entrada[4]), .Q(\Saída [4]));  // open: Qn, preset, en, reset
  D_Flip_Flop d_ff_18 (.clk(WR), .D(Entrada[12]), .Q(\Saída [12]));  // open: Qn, preset, en, reset
  D_Flip_Flop d_ff_19 (.clk(WR), .D(Entrada[20]), .Q(\Saída [20]));  // open: Qn, preset, en, reset
  D_Flip_Flop d_ff_20 (.clk(WR), .D(Entrada[28]), .Q(\Saída [28]));  // open: Qn, preset, en, reset
  D_Flip_Flop d_ff_21 (.clk(WR), .D(Entrada[5]), .Q(\Saída [5]));  // open: Qn, preset, en, reset
  D_Flip_Flop d_ff_22 (.clk(WR), .D(Entrada[13]), .Q(\Saída [13]));  // open: Qn, preset, en, reset
  D_Flip_Flop d_ff_23 (.clk(WR), .D(Entrada[21]), .Q(\Saída [21]));  // open: Qn, preset, en, reset
  D_Flip_Flop d_ff_24 (.clk(WR), .D(Entrada[29]), .Q(\Saída [29]));  // open: Qn, preset, en, reset
  D_Flip_Flop d_ff_25 (.clk(WR), .D(Entrada[6]), .Q(\Saída [6]));  // open: Qn, preset, en, reset
  D_Flip_Flop d_ff_26 (.clk(WR), .D(_14), .Q(\Saída [14]));  // open: Qn, preset, en, reset
  D_Flip_Flop d_ff_27 (.clk(WR), .D(Entrada[22]), .Q(\Saída [22]));  // open: Qn, preset, en, reset
  D_Flip_Flop d_ff_28 (.clk(WR), .D(Entrada[30]), .Q(\Saída [30]));  // open: Qn, preset, en, reset
  D_Flip_Flop d_ff_29 (.clk(WR), .D(Entrada[7]), .Q(\Saída [7]));  // open: Qn, preset, en, reset
  D_Flip_Flop d_ff_30 (.clk(WR), .D(Entrada[15]), .Q(\Saída [15]));  // open: Qn, preset, en, reset
  D_Flip_Flop d_ff_31 (.clk(WR), .D(Entrada[23]), .Q(\Saída [23]));  // open: Qn, preset, en, reset
  D_Flip_Flop d_ff_32 (.clk(WR), .D(Entrada[31]), .Q(\Saída [31]));  // open: Qn, preset, en, reset

  // Other names for the same wires on the sheet: E0 = Entrada[0]; E1 = Entrada[1]; E2 = Entrada[2]; E3 = Entrada[3];
  //   E4 = Entrada[4]; E5 = Entrada[5]; E6 = Entrada[6]; E7 = Entrada[7]; E8 = Entrada[8]; E9 = Entrada[9];
  //   E10 = Entrada[10]; E11 = Entrada[11]; E12 = Entrada[12]; E13 = Entrada[13]; E14 = Entrada[14];
  //   E15 = Entrada[15]; E16 = Entrada[16]; E17 = Entrada[17]; E18 = Entrada[18]; E19 = Entrada[19];
  //   E20 = Entrada[20]; E21 = Entrada[21]; E22 = Entrada[22]; E23 = Entrada[23]; E24 = Entrada[24];
  //   E25 = Entrada[25]; E26 = Entrada[26]; E27 = Entrada[27]; E28 = Entrada[28]; E29 = Entrada[29];
  //   E30 = Entrada[30]; E31 = Entrada[31]; S0 = \Saída [0]; S1 = \Saída [1]; S2 = \Saída [2]; S3 = \Saída [3];
  //   S4 = \Saída [4]; S5 = \Saída [5]; S6 = \Saída [6]; S7 = \Saída [7]; S8 = \Saída [8]; S9 = \Saída [9];
  //   S10 = \Saída [10]; S11 = \Saída [11]; S12 = \Saída [12]; S13 = \Saída [13]; S14 = \Saída [14];
  //   S15 = \Saída [15]; S16 = \Saída [16]; S17 = \Saída [17]; S18 = \Saída [18]; S19 = \Saída [19];
  //   S20 = \Saída [20]; S21 = \Saída [21]; S22 = \Saída [22]; S23 = \Saída [23]; S24 = \Saída [24];
  //   S25 = \Saída [25]; S26 = \Saída [26]; S27 = \Saída [27]; S28 = \Saída [28]; S29 = \Saída [29];
  //   S30 = \Saída [30]; S31 = \Saída [31]
endmodule

module BancoRegistradores (
  input  [31:0] DataIn,
  input  WR,
  input  [4:0] SelRegA,
  input  [4:0] SelRegW,
  input  [4:0] SelRegB,
  output [31:0] DataRegA,
  output [31:0] DataRegB
);

  wire W0, W1, W2, W3, W4, W5, W6, W7, W8, W9, W10, W11, W12, W13, W14, W15, W16, W17, W18, W19, W20, W21,
       W22, W23, W24, W25, W26, W27, W28, W29, W30, W31;
  wire [31:0] \registrador32bits_1_saída , \registrador32bits_2_saída , \registrador32bits_3_saída ,
       \registrador32bits_4_saída , \registrador32bits_5_saída , \registrador32bits_6_saída ,
       \registrador32bits_7_saída , \registrador32bits_8_saída , \registrador32bits_9_saída ,
       \registrador32bits_10_saída , \registrador32bits_11_saída , \registrador32bits_12_saída ,
       \registrador32bits_13_saída , \registrador32bits_14_saída , \registrador32bits_15_saída ,
       \registrador32bits_16_saída , \registrador32bits_17_saída , \registrador32bits_18_saída ,
       \registrador32bits_19_saída , \registrador32bits_20_saída , \registrador32bits_21_saída ,
       \registrador32bits_22_saída , \registrador32bits_23_saída , \registrador32bits_24_saída ,
       \registrador32bits_25_saída , \registrador32bits_26_saída , \registrador32bits_27_saída ,
       \registrador32bits_28_saída , \registrador32bits_29_saída , \registrador32bits_30_saída ,
       \registrador32bits_31_saída , \registrador32bits_32_saída ;

  Demultiplexer #(.select(5), .enable("false")) demultiplexer_1 (
    .out0(W0), .out1(W1), .out2(W2), .out3(W3), .out4(W4), .out5(W5), .out6(W6), .out7(W7), .out8(W8),
    .out9(W9), .out10(W10), .out11(W11), .out12(W12), .out13(W13), .out14(W14), .out15(W15), .out16(W16),
    .out17(W17), .out18(W18), .out19(W19), .out20(W20), .out21(W21), .out22(W22), .out23(W23), .out24(W24),
    .out25(W25), .out26(W26), .out27(W27), .out28(W28), .out29(W29), .out30(W30), .out31(W31), .in(WR),
    .sel(SelRegW));
  registrador32bits registrador32bits_1 (.WR(W0), .Entrada(DataIn), .\Saída (\registrador32bits_1_saída ));
  registrador32bits registrador32bits_2 (.WR(W4), .Entrada(DataIn), .\Saída (\registrador32bits_2_saída ));
  registrador32bits registrador32bits_3 (.WR(W8), .Entrada(DataIn), .\Saída (\registrador32bits_3_saída ));
  registrador32bits registrador32bits_4 (.WR(W12), .Entrada(DataIn), .\Saída (\registrador32bits_4_saída ));
  registrador32bits registrador32bits_5 (.WR(W16), .Entrada(DataIn), .\Saída (\registrador32bits_5_saída ));
  registrador32bits registrador32bits_6 (.WR(W20), .Entrada(DataIn), .\Saída (\registrador32bits_6_saída ));
  registrador32bits registrador32bits_7 (.WR(W24), .Entrada(DataIn), .\Saída (\registrador32bits_7_saída ));
  registrador32bits registrador32bits_8 (.WR(W28), .Entrada(DataIn), .\Saída (\registrador32bits_8_saída ));
  registrador32bits registrador32bits_9 (.WR(W1), .Entrada(DataIn), .\Saída (\registrador32bits_9_saída ));
  registrador32bits registrador32bits_10 (.WR(W5), .Entrada(DataIn), .\Saída (\registrador32bits_10_saída ));
  registrador32bits registrador32bits_11 (.WR(W9), .Entrada(DataIn), .\Saída (\registrador32bits_11_saída ));
  registrador32bits registrador32bits_12 (.WR(W13), .Entrada(DataIn), .\Saída (\registrador32bits_12_saída ));
  registrador32bits registrador32bits_13 (.WR(W17), .Entrada(DataIn), .\Saída (\registrador32bits_13_saída ));
  registrador32bits registrador32bits_14 (.WR(W21), .Entrada(DataIn), .\Saída (\registrador32bits_14_saída ));
  registrador32bits registrador32bits_15 (.WR(W25), .Entrada(DataIn), .\Saída (\registrador32bits_15_saída ));
  registrador32bits registrador32bits_16 (.WR(W29), .Entrada(DataIn), .\Saída (\registrador32bits_16_saída ));
  registrador32bits registrador32bits_17 (.WR(W2), .Entrada(DataIn), .\Saída (\registrador32bits_17_saída ));
  registrador32bits registrador32bits_18 (.WR(W6), .Entrada(DataIn), .\Saída (\registrador32bits_18_saída ));
  registrador32bits registrador32bits_19 (.WR(W10), .Entrada(DataIn), .\Saída (\registrador32bits_19_saída ));
  registrador32bits registrador32bits_20 (.WR(W14), .Entrada(DataIn), .\Saída (\registrador32bits_20_saída ));
  registrador32bits registrador32bits_21 (.WR(W18), .Entrada(DataIn), .\Saída (\registrador32bits_21_saída ));
  registrador32bits registrador32bits_22 (.WR(W22), .Entrada(DataIn), .\Saída (\registrador32bits_22_saída ));
  registrador32bits registrador32bits_23 (.WR(W26), .Entrada(DataIn), .\Saída (\registrador32bits_23_saída ));
  registrador32bits registrador32bits_24 (.WR(W30), .Entrada(DataIn), .\Saída (\registrador32bits_24_saída ));
  registrador32bits registrador32bits_25 (.WR(W3), .Entrada(DataIn), .\Saída (\registrador32bits_25_saída ));
  registrador32bits registrador32bits_26 (.WR(W7), .Entrada(DataIn), .\Saída (\registrador32bits_26_saída ));
  registrador32bits registrador32bits_27 (.WR(W11), .Entrada(DataIn), .\Saída (\registrador32bits_27_saída ));
  registrador32bits registrador32bits_28 (.WR(W15), .Entrada(DataIn), .\Saída (\registrador32bits_28_saída ));
  registrador32bits registrador32bits_29 (.WR(W19), .Entrada(DataIn), .\Saída (\registrador32bits_29_saída ));
  registrador32bits registrador32bits_30 (.WR(W23), .Entrada(DataIn), .\Saída (\registrador32bits_30_saída ));
  registrador32bits registrador32bits_31 (.WR(W27), .Entrada(DataIn), .\Saída (\registrador32bits_31_saída ));
  registrador32bits registrador32bits_32 (.WR(W31), .Entrada(DataIn), .\Saída (\registrador32bits_32_saída ));
  Multiplexer #(.select(5), .width(32), .enable("false")) multiplexer_1 (
    .in0(\registrador32bits_1_saída ), .in1(\registrador32bits_9_saída ), .in2(\registrador32bits_17_saída ),
    .in3(\registrador32bits_25_saída ), .in4(\registrador32bits_2_saída ),
    .in5(\registrador32bits_10_saída ), .in6(\registrador32bits_18_saída ),
    .in7(\registrador32bits_26_saída ), .in8(\registrador32bits_3_saída ),
    .in9(\registrador32bits_11_saída ), .in10(\registrador32bits_19_saída ),
    .in11(\registrador32bits_27_saída ), .in12(\registrador32bits_4_saída ),
    .in13(\registrador32bits_12_saída ), .in14(\registrador32bits_20_saída ),
    .in15(\registrador32bits_28_saída ), .in16(\registrador32bits_5_saída ),
    .in17(\registrador32bits_13_saída ), .in18(\registrador32bits_21_saída ),
    .in19(\registrador32bits_29_saída ), .in20(\registrador32bits_6_saída ),
    .in21(\registrador32bits_14_saída ), .in22(\registrador32bits_22_saída ),
    .in23(\registrador32bits_30_saída ), .in24(\registrador32bits_7_saída ),
    .in25(\registrador32bits_15_saída ), .in26(\registrador32bits_23_saída ),
    .in27(\registrador32bits_31_saída ), .in28(\registrador32bits_8_saída ),
    .in29(\registrador32bits_16_saída ), .in30(\registrador32bits_24_saída ),
    .in31(\registrador32bits_32_saída ), .out(DataRegA), .sel(SelRegA));
  Multiplexer #(.select(5), .width(32), .enable("false")) multiplexer_2 (
    .in0(\registrador32bits_1_saída ), .in1(\registrador32bits_9_saída ), .in2(\registrador32bits_17_saída ),
    .in3(\registrador32bits_25_saída ), .in4(\registrador32bits_2_saída ),
    .in5(\registrador32bits_10_saída ), .in6(\registrador32bits_18_saída ),
    .in7(\registrador32bits_26_saída ), .in8(\registrador32bits_3_saída ),
    .in9(\registrador32bits_11_saída ), .in10(\registrador32bits_19_saída ),
    .in11(\registrador32bits_27_saída ), .in12(\registrador32bits_4_saída ),
    .in13(\registrador32bits_12_saída ), .in14(\registrador32bits_20_saída ),
    .in15(\registrador32bits_28_saída ), .in16(\registrador32bits_5_saída ),
    .in17(\registrador32bits_13_saída ), .in18(\registrador32bits_21_saída ),
    .in19(\registrador32bits_29_saída ), .in20(\registrador32bits_6_saída ),
    .in21(\registrador32bits_14_saída ), .in22(\registrador32bits_22_saída ),
    .in23(\registrador32bits_30_saída ), .in24(\registrador32bits_7_saída ),
    .in25(\registrador32bits_15_saída ), .in26(\registrador32bits_23_saída ),
    .in27(\registrador32bits_31_saída ), .in28(\registrador32bits_8_saída ),
    .in29(\registrador32bits_16_saída ), .in30(\registrador32bits_24_saída ),
    .in31(\registrador32bits_32_saída ), .out(DataRegB), .sel(SelRegB));
endmodule

module ULAReg (
  input  WR,
  input  [3:0] OperCode,
  input  [4:0] SelRegW,
  input  [4:0] SelRegA,
  input  [4:0] SelRegB
);

  wire [31:0] bancoregistradores_1_datarega, bancoregistradores_1_dataregb, \ula_1_saída ;

  BancoRegistradores bancoregistradores_1 (
    .WR(WR), .DataIn(\ula_1_saída ), .SelRegW(SelRegW), .SelRegA(SelRegA), .SelRegB(SelRegB),
    .DataRegA(bancoregistradores_1_datarega), .DataRegB(bancoregistradores_1_dataregb));
  ULA ula_1 (
    .A(bancoregistradores_1_datarega), .B(bancoregistradores_1_dataregb), .\Saída (\ula_1_saída ),
    .OperCode(OperCode));  // open: out_5
endmodule
