// Logisim project Somador Completo.circ as structural Verilog: 2 circuits, main circuit main
module main (
);

  SomadorCompleto somadorcompleto_1 ();  // open: in_1, in_2, in_3, out_4, out_5
endmodule

module SomadorCompleto (
  input  in_1,
  input  in_2,
  input  in_3,
  output out_4,
  output out_5
);

  wire and_1_out, and_2_out, and_3_out;

  ExactlyOne xor_1 (.out(out_5), .in0(in_2), .in1(in_1), .in2(in_3));
  and and_1 (and_1_out, in_1, in_2);
  and and_2 (and_2_out, in_3, in_2);
  and and_3 (and_3_out, in_3, in_1);
  or or_1 (out_4, and_1_out, and_2_out, and_3_out);
endmodule
