// Logisim project ULA32Bits.circ as structural Verilog
module mux16 (
  input  in_1,
  input  in_2,
  input  in_3,
  input  in_4,
  input  in_5,
  input  in_6,
  input  in_7,
  input  in_8,
  input  in_9,
  input  in_10,
  input  in_11,
  input  in_12,
  input  in_13,
  input  in_14,
  input  in_15,
  input  in_16,
  input  [3:0] Sel,
  output out_18
);

  wire and_1_out, and_2_out, and_3_out, and_4_out, and_5_out, and_6_out, and_7_out, and_8_out, and_9_out,
       and_10_out, and_11_out, and_12_out, and_13_out, and_14_out, and_15_out, and_16_out;

  and and_1 (and_1_out, in_1, ~Sel[3], ~Sel[2], ~Sel[1], ~Sel[0]);  // AND_Gate
  and and_2 (and_2_out, in_2, ~Sel[3], ~Sel[2], ~Sel[1], Sel[0]);  // AND_Gate
  and and_3 (and_3_out, in_3, ~Sel[3], ~Sel[2], Sel[1], ~Sel[0]);  // AND_Gate
  and and_4 (and_4_out, in_4, ~Sel[3], ~Sel[2], Sel[1], Sel[0]);  // AND_Gate
  and and_5 (and_5_out, in_5, ~Sel[3], Sel[2], ~Sel[1], ~Sel[0]);  // AND_Gate
  and and_6 (and_6_out, in_6, ~Sel[3], Sel[2], ~Sel[1], Sel[0]);  // AND_Gate
  and and_7 (and_7_out, in_7, ~Sel[3], Sel[2], Sel[1], ~Sel[0]);  // AND_Gate
  and and_8 (and_8_out, in_8, ~Sel[3], Sel[2], Sel[1], Sel[0]);  // AND_Gate
  and and_9 (and_9_out, in_9, Sel[3], ~Sel[2], ~Sel[1], ~Sel[0]);  // AND_Gate
  and and_10 (and_10_out, in_10, Sel[3], ~Sel[2], ~Sel[1], Sel[0]);  // AND_Gate
  and and_11 (and_11_out, in_11, Sel[3], ~Sel[2], Sel[1], ~Sel[0]);  // AND_Gate
  and and_12 (and_12_out, in_12, Sel[3], ~Sel[2], Sel[1], Sel[0]);  // AND_Gate
  and and_13 (and_13_out, in_13, Sel[3], Sel[2], ~Sel[1], ~Sel[0]);  // AND_Gate
  and and_14 (and_14_out, in_14, Sel[3], Sel[2], ~Sel[1], Sel[0]);  // AND_Gate
  and and_15 (and_15_out, in_15, Sel[3], Sel[2], Sel[1], ~Sel[0]);  // AND_Gate
  and and_16 (and_16_out, in_16, Sel[3], Sel[2], Sel[1], Sel[0]);
  or or_1 (out_18, and_1_out, and_2_out, and_3_out, and_4_out, and_5_out, and_6_out, and_7_out, and_8_out, and_9_out, and_10_out, and_11_out, and_12_out, and_13_out, and_14_out, and_15_out, and_16_out);
endmodule

module ULACell (
  input  B,
  input  A,
  input  [3:0] SelectorOperador,
  input  vem1_plus,
  input  vem1_minus,
  output \Saída ,
  output vai1_plus,
  output vai1_minus
);

  wire and_1_out, or_1_out, somc_1_soma, sub_1_soma, xor_1_out;

  and and_1 (and_1_out, A, B);
  or or_1 (or_1_out, A, B);
  xor xor_1 (xor_1_out, A, B);
  SomC somc_1 (.Vai1(vai1_plus), .B(B), .A(A), .Soma(somc_1_soma), .V1(vem1_plus));
  Sub sub_1 (.Vai1(vai1_minus), .B(B), .A(A), .Soma(sub_1_soma), .V1(vem1_minus));
  mux16 mux16_1 (
    .in_1(and_1_out), .in_2(or_1_out), .in_3(xor_1_out), .in_4(somc_1_soma), .in_5(sub_1_soma), .in_6(B),
    .in_7(B), .in_8(B), .in_9(B), .Sel(SelectorOperador), .out_18(\Saída ));  // open: in_10, in_11, in_12, in_13, in_14, in_15, in_16
endmodule

module SomC (
  input  B,
  input  A,
  input  V1,
  output Vai1,
  output Soma
);

  wire and_1_out, and_2_out, and_3_out, xor_1_out;

  or or_1 (Vai1, and_1_out, and_2_out, and_3_out);
  and and_1 (and_1_out, V1, B);
  and and_2 (and_2_out, B, A);
  and and_3 (and_3_out, A, V1);
  xor xor_1 (xor_1_out, A, B);
  xor xor_2 (Soma, xor_1_out, V1);
endmodule

module ULA (
  input  [31:0] A,
  input  [31:0] B,
  input  [3:0] in_3,
  output out_4,
  output out_5,
  output [31:0] out_6
);

  wire sleft1bit_detector_1_out_2, sright1bit_detector_1_out_2, srighta1bit_detector_1_out_2,
       ulacell_2_vai1_minus, ulacell_2_vai1_plus, ulacell_3_vai1_minus, ulacell_3_vai1_plus,
       ulacell_4_vai1_minus, ulacell_4_vai1_plus, ulacell_5_vai1_minus, ulacell_5_vai1_plus,
       ulacell_6_vai1_minus, ulacell_6_vai1_plus, ulacell_7_vai1_minus, ulacell_7_vai1_plus,
       ulacell_8_vai1_minus, ulacell_8_vai1_plus, ulacell_9_vai1_minus, ulacell_9_vai1_plus,
       ulacell_10_vai1_minus, ulacell_10_vai1_plus, ulacell_11_vai1_minus, ulacell_11_vai1_plus,
       ulacell_12_vai1_minus, ulacell_12_vai1_plus, ulacell_13_vai1_minus, ulacell_13_vai1_plus,
       ulacell_14_vai1_minus, ulacell_14_vai1_plus, ulacell_15_vai1_minus, ulacell_15_vai1_plus,
       ulacell_16_vai1_minus, ulacell_16_vai1_plus, ulacell_17_vai1_minus, ulacell_17_vai1_plus,
       ulacell_18_vai1_minus, ulacell_18_vai1_plus, ulacell_19_vai1_minus, ulacell_19_vai1_plus,
       ulacell_20_vai1_minus, ulacell_20_vai1_plus, ulacell_21_vai1_minus, ulacell_21_vai1_plus,
       ulacell_22_vai1_minus, ulacell_22_vai1_plus, ulacell_23_vai1_minus, ulacell_23_vai1_plus,
       ulacell_24_vai1_minus, ulacell_24_vai1_plus, ulacell_25_vai1_minus, ulacell_25_vai1_plus,
       ulacell_26_vai1_minus, ulacell_26_vai1_plus, ulacell_27_vai1_minus, ulacell_27_vai1_plus,
       ulacell_28_vai1_minus, ulacell_28_vai1_plus, ulacell_29_vai1_minus, ulacell_29_vai1_plus,
       ulacell_30_vai1_minus, ulacell_30_vai1_plus, ulacell_31_vai1_minus, ulacell_31_vai1_plus,
       ulacell_32_vai1_minus, ulacell_32_vai1_plus;
  wire [31:0] sleftl1bit_1_out_3, srighta1bit_1_out_3, srightl1bit_1_out_3;

  SleftL1bit sleftl1bit_1 (.in_1(B), .Shift(sleft1bit_detector_1_out_2), .out_3(sleftl1bit_1_out_3));
  Sright1bit_detector sright1bit_detector_1 (.out_2(sright1bit_detector_1_out_2), .in_1(in_3));
  Sleft1bit_detector sleft1bit_detector_1 (.out_2(sleft1bit_detector_1_out_2), .in_1(in_3));
  SrightA1bit srighta1bit_1 (
    .in_1(srightl1bit_1_out_3), .Shift(srighta1bit_detector_1_out_2), .out_3(srighta1bit_1_out_3));
  SrightL1bit srightl1bit_1 (
    .in_1(sleftl1bit_1_out_3), .Shift(sright1bit_detector_1_out_2), .out_3(srightl1bit_1_out_3));
  SrightA1bit_detector srighta1bit_detector_1 (.out_2(srighta1bit_detector_1_out_2), .in_1(in_3));
  ULACell ulacell_1 (
    .vai1_plus(out_4), .vai1_minus(out_5), .\Saída (out_6[31]), .vem1_plus(ulacell_3_vai1_plus),
    .vem1_minus(ulacell_3_vai1_minus), .B(srighta1bit_1_out_3[31]), .A(A[31]), .SelectorOperador(in_3));
  ULACell ulacell_2 (
    .vai1_plus(ulacell_2_vai1_plus), .vai1_minus(ulacell_2_vai1_minus), .\Saída (out_6[29]),
    .vem1_plus(ulacell_4_vai1_plus), .vem1_minus(ulacell_4_vai1_minus), .B(srighta1bit_1_out_3[29]),
    .A(A[29]), .SelectorOperador(in_3));
  ULACell ulacell_3 (
    .vai1_plus(ulacell_3_vai1_plus), .vai1_minus(ulacell_3_vai1_minus), .\Saída (out_6[30]),
    .vem1_plus(ulacell_2_vai1_plus), .vem1_minus(ulacell_2_vai1_minus), .B(srighta1bit_1_out_3[30]),
    .A(A[30]), .SelectorOperador(in_3));
  ULACell ulacell_4 (
    .vai1_plus(ulacell_4_vai1_plus), .vai1_minus(ulacell_4_vai1_minus), .\Saída (out_6[28]),
    .vem1_plus(ulacell_5_vai1_plus), .vem1_minus(ulacell_5_vai1_minus), .B(srighta1bit_1_out_3[28]),
    .A(A[28]), .SelectorOperador(in_3));
  ULACell ulacell_5 (
    .vai1_plus(ulacell_5_vai1_plus), .vai1_minus(ulacell_5_vai1_minus), .\Saída (out_6[27]),
    .vem1_plus(ulacell_7_vai1_plus), .vem1_minus(ulacell_7_vai1_minus), .B(srighta1bit_1_out_3[27]),
    .A(A[27]), .SelectorOperador(in_3));
  ULACell ulacell_6 (
    .vai1_plus(ulacell_6_vai1_plus), .vai1_minus(ulacell_6_vai1_minus), .\Saída (out_6[25]),
    .vem1_plus(ulacell_8_vai1_plus), .vem1_minus(ulacell_8_vai1_minus), .B(srighta1bit_1_out_3[25]),
    .A(A[25]), .SelectorOperador(in_3));
  ULACell ulacell_7 (
    .vai1_plus(ulacell_7_vai1_plus), .vai1_minus(ulacell_7_vai1_minus), .\Saída (out_6[26]),
    .vem1_plus(ulacell_6_vai1_plus), .vem1_minus(ulacell_6_vai1_minus), .B(srighta1bit_1_out_3[26]),
    .A(A[26]), .SelectorOperador(in_3));
  ULACell ulacell_8 (
    .vai1_plus(ulacell_8_vai1_plus), .vai1_minus(ulacell_8_vai1_minus), .\Saída (out_6[24]),
    .vem1_plus(ulacell_9_vai1_plus), .vem1_minus(ulacell_9_vai1_minus), .B(srighta1bit_1_out_3[24]),
    .A(A[24]), .SelectorOperador(in_3));
  ULACell ulacell_9 (
    .vai1_plus(ulacell_9_vai1_plus), .vai1_minus(ulacell_9_vai1_minus), .\Saída (out_6[23]),
    .vem1_plus(ulacell_11_vai1_plus), .vem1_minus(ulacell_11_vai1_minus), .B(srighta1bit_1_out_3[23]),
    .A(A[23]), .SelectorOperador(in_3));
  ULACell ulacell_10 (
    .vai1_plus(ulacell_10_vai1_plus), .vai1_minus(ulacell_10_vai1_minus), .\Saída (out_6[21]),
    .vem1_plus(ulacell_12_vai1_plus), .vem1_minus(ulacell_12_vai1_minus), .B(srighta1bit_1_out_3[21]),
    .A(A[21]), .SelectorOperador(in_3));
  ULACell ulacell_11 (
    .vai1_plus(ulacell_11_vai1_plus), .vai1_minus(ulacell_11_vai1_minus), .\Saída (out_6[22]),
    .vem1_plus(ulacell_10_vai1_plus), .vem1_minus(ulacell_10_vai1_minus), .B(srighta1bit_1_out_3[22]),
    .A(A[22]), .SelectorOperador(in_3));
  ULACell ulacell_12 (
    .vai1_plus(ulacell_12_vai1_plus), .vai1_minus(ulacell_12_vai1_minus), .\Saída (out_6[20]),
    .vem1_plus(ulacell_13_vai1_plus), .vem1_minus(ulacell_13_vai1_minus), .B(srighta1bit_1_out_3[20]),
    .A(A[20]), .SelectorOperador(in_3));
  ULACell ulacell_13 (
    .vai1_plus(ulacell_13_vai1_plus), .vai1_minus(ulacell_13_vai1_minus), .\Saída (out_6[19]),
    .vem1_plus(ulacell_15_vai1_plus), .vem1_minus(ulacell_15_vai1_minus), .B(srighta1bit_1_out_3[19]),
    .A(A[19]), .SelectorOperador(in_3));
  ULACell ulacell_14 (
    .vai1_plus(ulacell_14_vai1_plus), .vai1_minus(ulacell_14_vai1_minus), .\Saída (out_6[17]),
    .vem1_plus(ulacell_16_vai1_plus), .vem1_minus(ulacell_16_vai1_minus), .B(srighta1bit_1_out_3[17]),
    .A(A[17]), .SelectorOperador(in_3));
  ULACell ulacell_15 (
    .vai1_plus(ulacell_15_vai1_plus), .vai1_minus(ulacell_15_vai1_minus), .\Saída (out_6[18]),
    .vem1_plus(ulacell_14_vai1_plus), .vem1_minus(ulacell_14_vai1_minus), .B(srighta1bit_1_out_3[18]),
    .A(A[18]), .SelectorOperador(in_3));
  ULACell ulacell_16 (
    .vai1_plus(ulacell_16_vai1_plus), .vai1_minus(ulacell_16_vai1_minus), .\Saída (out_6[16]),
    .vem1_plus(ulacell_17_vai1_plus), .vem1_minus(ulacell_17_vai1_minus), .B(srighta1bit_1_out_3[16]),
    .A(A[16]), .SelectorOperador(in_3));
  ULACell ulacell_17 (
    .vai1_plus(ulacell_17_vai1_plus), .vai1_minus(ulacell_17_vai1_minus), .\Saída (out_6[15]),
    .vem1_plus(ulacell_19_vai1_plus), .vem1_minus(ulacell_19_vai1_minus), .B(srighta1bit_1_out_3[15]),
    .A(A[15]), .SelectorOperador(in_3));
  ULACell ulacell_18 (
    .vai1_plus(ulacell_18_vai1_plus), .vai1_minus(ulacell_18_vai1_minus), .\Saída (out_6[13]),
    .vem1_plus(ulacell_20_vai1_plus), .vem1_minus(ulacell_20_vai1_minus), .B(srighta1bit_1_out_3[13]),
    .A(A[13]), .SelectorOperador(in_3));
  ULACell ulacell_19 (
    .vai1_plus(ulacell_19_vai1_plus), .vai1_minus(ulacell_19_vai1_minus), .\Saída (out_6[14]),
    .vem1_plus(ulacell_18_vai1_plus), .vem1_minus(ulacell_18_vai1_minus), .B(srighta1bit_1_out_3[14]),
    .A(A[14]), .SelectorOperador(in_3));
  ULACell ulacell_20 (
    .vai1_plus(ulacell_20_vai1_plus), .vai1_minus(ulacell_20_vai1_minus), .\Saída (out_6[12]),
    .vem1_plus(ulacell_21_vai1_plus), .vem1_minus(ulacell_21_vai1_minus), .B(srighta1bit_1_out_3[12]),
    .A(A[12]), .SelectorOperador(in_3));
  ULACell ulacell_21 (
    .vai1_plus(ulacell_21_vai1_plus), .vai1_minus(ulacell_21_vai1_minus), .\Saída (out_6[11]),
    .vem1_plus(ulacell_22_vai1_plus), .vem1_minus(ulacell_22_vai1_minus), .B(srighta1bit_1_out_3[11]),
    .A(A[11]), .SelectorOperador(in_3));
  ULACell ulacell_22 (
    .vai1_plus(ulacell_22_vai1_plus), .vai1_minus(ulacell_22_vai1_minus), .\Saída (out_6[10]),
    .vem1_plus(ulacell_23_vai1_plus), .vem1_minus(ulacell_23_vai1_minus), .B(srighta1bit_1_out_3[10]),
    .A(A[10]), .SelectorOperador(in_3));
  ULACell ulacell_23 (
    .vai1_plus(ulacell_23_vai1_plus), .vai1_minus(ulacell_23_vai1_minus), .\Saída (out_6[9]),
    .vem1_plus(ulacell_24_vai1_plus), .vem1_minus(ulacell_24_vai1_minus), .B(srighta1bit_1_out_3[9]),
    .A(A[9]), .SelectorOperador(in_3));
  ULACell ulacell_24 (
    .vai1_plus(ulacell_24_vai1_plus), .vai1_minus(ulacell_24_vai1_minus), .\Saída (out_6[8]),
    .vem1_plus(ulacell_25_vai1_plus), .vem1_minus(ulacell_25_vai1_minus), .B(srighta1bit_1_out_3[8]),
    .A(A[8]), .SelectorOperador(in_3));
  ULACell ulacell_25 (
    .vai1_plus(ulacell_25_vai1_plus), .vai1_minus(ulacell_25_vai1_minus), .\Saída (out_6[7]),
    .vem1_plus(ulacell_26_vai1_plus), .vem1_minus(ulacell_26_vai1_minus), .B(srighta1bit_1_out_3[7]),
    .A(A[7]), .SelectorOperador(in_3));
  ULACell ulacell_26 (
    .vai1_plus(ulacell_26_vai1_plus), .vai1_minus(ulacell_26_vai1_minus), .\Saída (out_6[6]),
    .vem1_plus(ulacell_27_vai1_plus), .vem1_minus(ulacell_27_vai1_minus), .B(srighta1bit_1_out_3[6]),
    .A(A[6]), .SelectorOperador(in_3));
  ULACell ulacell_27 (
    .vai1_plus(ulacell_27_vai1_plus), .vai1_minus(ulacell_27_vai1_minus), .\Saída (out_6[5]),
    .vem1_plus(ulacell_28_vai1_plus), .vem1_minus(ulacell_28_vai1_minus), .B(srighta1bit_1_out_3[5]),
    .A(A[5]), .SelectorOperador(in_3));
  ULACell ulacell_28 (
    .vai1_plus(ulacell_28_vai1_plus), .vai1_minus(ulacell_28_vai1_minus), .\Saída (out_6[4]),
    .vem1_plus(ulacell_29_vai1_plus), .vem1_minus(ulacell_29_vai1_minus), .B(srighta1bit_1_out_3[4]),
    .A(A[4]), .SelectorOperador(in_3));
  ULACell ulacell_29 (
    .vai1_plus(ulacell_29_vai1_plus), .vai1_minus(ulacell_29_vai1_minus), .\Saída (out_6[3]),
    .vem1_plus(ulacell_30_vai1_plus), .vem1_minus(ulacell_30_vai1_minus), .B(srighta1bit_1_out_3[3]),
    .A(A[3]), .SelectorOperador(in_3));
  ULACell ulacell_30 (
    .vai1_plus(ulacell_30_vai1_plus), .vai1_minus(ulacell_30_vai1_minus), .\Saída (out_6[2]),
    .vem1_plus(ulacell_31_vai1_plus), .vem1_minus(ulacell_31_vai1_minus), .B(srighta1bit_1_out_3[2]),
    .A(A[2]), .SelectorOperador(in_3));
  ULACell ulacell_31 (
    .vai1_plus(ulacell_31_vai1_plus), .vai1_minus(ulacell_31_vai1_minus), .\Saída (out_6[1]),
    .vem1_plus(ulacell_32_vai1_plus), .vem1_minus(ulacell_32_vai1_minus), .B(srighta1bit_1_out_3[1]),
    .A(A[1]), .SelectorOperador(in_3));
  ULACell ulacell_32 (
    .vai1_plus(ulacell_32_vai1_plus), .vai1_minus(ulacell_32_vai1_minus), .\Saída (out_6[0]),
    .vem1_plus(1'b0), .vem1_minus(1'b0), .B(srighta1bit_1_out_3[0]), .A(A[0]), .SelectorOperador(in_3));
endmodule

module Sub (
  input  B,
  input  A,
  input  V1,
  output Vai1,
  output Soma
);

  wire and_1_out, and_2_out, and_3_out, xor_1_out;

  or or_1 (Vai1, and_1_out, and_2_out, and_3_out);
  and and_1 (and_1_out, V1, B);
  and and_2 (and_2_out, B, ~A);  // AND_Gate
  and and_3 (and_3_out, ~A, V1);  // AND_Gate
  xor xor_1 (xor_1_out, A, B);
  xor xor_2 (Soma, xor_1_out, V1);
endmodule

module SleftL1bit (
  input  [31:0] in_1,
  input  Shift,
  output [31:0] out_3
);

  Multiplexer #(.width(32), .enable("false")) multiplexer_1 (
    .in0(in_1), .in1({in_1[30:0], 1'b0}), .out(out_3), .sel(Shift));
endmodule

module SrightL1bit (
  input  [31:0] in_1,
  input  Shift,
  output [31:0] out_3
);

  Multiplexer #(.width(32), .enable("false")) multiplexer_1 (
    .in0(in_1), .in1({1'b0, in_1[31:1]}), .out(out_3), .sel(Shift));
endmodule

module SrightA1bit (
  input  [31:0] in_1,
  input  Shift,
  output [31:0] out_3
);

  Multiplexer #(.width(32), .enable("false")) multiplexer_1 (
    .in0(in_1), .in1({{2{in_1[31]}}, in_1[30:1]}), .out(out_3), .sel(Shift));
endmodule

module SleftA1bit (
  input  [31:0] in_1,
  input  Shift,
  output [31:0] out_3
);

  Multiplexer #(.width(32), .enable("false")) multiplexer_1 (
    .in0(in_1), .in1({in_1[30:0], in_1[0]}), .out(out_3), .sel(Shift));
endmodule

module Sleft1bit_detector (
  input  [3:0] in_1,
  output out_2
);

  and and_1 (out_2, ~in_1[3], in_1[2], in_1[1], ~in_1[0]);  // AND_Gate
endmodule

module Sright1bit_detector (
  input  [3:0] in_1,
  output out_2
);

  and and_1 (out_2, ~in_1[3], in_1[2], in_1[1], in_1[0]);  // AND_Gate
endmodule

module SrightA1bit_detector (
  input  [3:0] in_1,
  output out_2
);

  and and_1 (out_2, in_1[3], ~in_1[2], ~in_1[1], ~in_1[0]);  // AND_Gate
endmodule
